// Logisim project Final_Project.circ as structural Verilog: 5 circuits, main circuit Final_TopLevel
module Final_TopLevel (
);

  wire button_1_out, button_2_out, clock_1_out, final_control_1_en, final_control_1_g, final_control_1_load,
       final_control_1_updown, final_core_1_ledeight, final_core_1_ledone, final_core_1_out_7,
       final_core_1_out_8, final_core_1_out_9, final_core_1_out_10, final_core_1_out_11, final_core_1_out_12,
       final_core_1_qd;

  Button button_1 (.out(button_1_out));
  Button button_2 (.out(button_2_out));
  Final_Control final_control_1 (
    .PlayerOne(button_1_out), .LedOne(final_core_1_ledone), .LedEight(final_core_1_ledeight),
    .QD(final_core_1_qd), .ResetOne(button_2_out), .UpDown(final_control_1_updown),
    .Load(final_control_1_load), .En(final_control_1_en), .G(final_control_1_g));
  Clock clock_1 (.out(clock_1_out));
  Final_Core final_core_1 (
    .UpDown(final_control_1_updown), .Load(final_control_1_load), .En(final_control_1_en),
    .G(final_control_1_g), .CLK(clock_1_out), .LedOne(final_core_1_ledone), .out_7(final_core_1_out_7),
    .out_8(final_core_1_out_8), .out_9(final_core_1_out_9), .out_10(final_core_1_out_10),
    .out_11(final_core_1_out_11), .out_12(final_core_1_out_12), .LedEight(final_core_1_ledeight),
    .QD(final_core_1_qd));
  LED led_1 (.in(final_core_1_ledone));
  LED led_2 (.in(final_core_1_out_7));
  LED led_3 (.in(final_core_1_out_8));
  LED led_4 (.in(final_core_1_out_9));
  LED led_5 (.in(final_core_1_out_10));
  LED led_6 (.in(final_core_1_out_11));
  LED led_7 (.in(final_core_1_out_12));
  LED led_8 (.in(final_core_1_ledeight));
endmodule

module Final_Core (
  input  UpDown,
  input  Load,
  input  En,
  input  G,
  input  CLK,
  output LedOne,
  output out_7,
  output out_8,
  output out_9,
  output out_10,
  output out_11,
  output out_12,
  output LedEight,
  output QD
);

  wire sn74155_1_y10, sn74155_1_y11, sn74155_1_y12, sn74155_1_y13, sn74155_1_y20, sn74155_1_y21,
       sn74155_1_y22, sn74155_1_y23, sn74191_1_outa, sn74191_1_outb, sn74191_1_outc;

  SN74191 sn74191_1 (
    .DownUp(UpDown), .CTEN(En), .DataA(1'b0), .DataB(1'b0), .DataC(1'b0), .DataD(1'b0), .Load(Load),
    .CLK(CLK), .OutA(sn74191_1_outa), .OutB(sn74191_1_outb), .OutC(sn74191_1_outc), .OutD(QD));  // open: MaxMin
  SN74155 sn74155_1 (
    .SelectA(sn74191_1_outa), .SelectB(sn74191_1_outb), .C1(sn74191_1_outc), .C2(sn74191_1_outc), .G1(G),
    .G2(G), .Y20(sn74155_1_y20), .Y21(sn74155_1_y21), .Y22(sn74155_1_y22), .Y23(sn74155_1_y23),
    .Y10(sn74155_1_y10), .Y11(sn74155_1_y11), .Y12(sn74155_1_y12), .Y13(sn74155_1_y13));
  not not_1 (LedOne, sn74155_1_y20);
  not not_2 (out_7, sn74155_1_y21);
  not not_3 (out_8, sn74155_1_y22);
  not not_4 (out_9, sn74155_1_y23);
  not not_5 (out_10, sn74155_1_y10);
  not not_6 (out_11, sn74155_1_y11);
  not not_7 (out_12, sn74155_1_y12);
  not not_8 (LedEight, sn74155_1_y13);
endmodule

module SN74191 (
  input  DownUp,
  input  CTEN,
  input  DataA,
  input  DataB,
  input  DataC,
  input  DataD,
  input  Load,
  input  CLK,
  output MaxMin,
  output OutA,
  output OutB,
  output OutC,
  output OutD
);

  wire and_1_out, and_2_out, and_3_out, and_4_out, and_5_out, and_6_out, and_7_out, and_8_out, and_9_out,
       and_10_out, nand_1_out, nand_2_out, nand_3_out, nand_4_out, nand_5_out, nand_6_out, nand_7_out,
       nand_8_out, not_1_out, not_2_out, not_3_out, not_4_out, not_5_out, not_6_out, not_7_out, not_8_out,
       not_9_out, not_10_out, not_11_out, not_12_out, not_13_out, not_14_out, not_15_out, not_16_out,
       not_17_out, not_18_out, not_19_out, not_20_out, not_21_out, or_2_out, or_3_out, or_4_out, t_ff_1_qn,
       t_ff_2_qn, t_ff_3_qn, t_ff_4_qn;

  not not_1 (not_1_out, not_8_out);
  not not_2 (not_2_out, CTEN);
  not not_3 (not_3_out, CTEN);
  not not_4 (not_4_out, not_7_out);
  not not_5 (not_5_out, Load);
  not not_6 (not_6_out, CLK);
  not not_7 (not_7_out, DownUp);
  and and_1 (and_1_out, not_1_out, not_2_out);
  and and_2 (and_2_out, not_3_out, not_4_out);
  not not_8 (not_8_out, not_7_out);
  not not_9 (not_9_out, CTEN);
  and and_3 (and_3_out, not_7_out, OutA, OutB, OutC, OutD);
  and and_4 (and_4_out, not_8_out, t_ff_1_qn, t_ff_2_qn, t_ff_3_qn, t_ff_4_qn);
  nand nand_1 (nand_1_out, not_5_out, DataB);
  and and_5 (and_5_out, and_2_out, t_ff_1_qn);
  and and_6 (and_6_out, OutA, and_1_out);
  nand nand_2 (nand_2_out, not_5_out, DataC);
  and and_7 (and_7_out, and_2_out, t_ff_1_qn, t_ff_2_qn);
  and and_8 (and_8_out, OutA, OutB, and_1_out);
  nand nand_3 (nand_3_out, not_5_out, DataD);
  and and_9 (and_9_out, and_2_out, t_ff_1_qn, t_ff_2_qn, t_ff_3_qn);
  and and_10 (and_10_out, OutA, OutB, OutC, and_1_out);
  or or_1 (MaxMin, and_3_out, and_4_out);
  nand nand_4 (nand_4_out, not_5_out, DataA);
  or or_2 (or_2_out, and_5_out, and_6_out);
  or or_3 (or_3_out, and_7_out, and_8_out);
  or or_4 (or_4_out, and_9_out, and_10_out);
  nand nand_5 (nand_5_out, nand_4_out, not_5_out);
  nand nand_6 (nand_6_out, nand_1_out, not_5_out);
  not not_10 (not_10_out, nand_4_out);
  T_Flip_Flop t_ff_1 (
    .T(not_9_out), .clk(not_11_out), .Q(OutA), .Qn(t_ff_1_qn), .reset(not_12_out), .preset(not_10_out));
  not not_11 (not_11_out, not_6_out);
  not not_12 (not_12_out, nand_5_out);
  not not_13 (not_13_out, nand_1_out);
  T_Flip_Flop t_ff_2 (
    .T(or_2_out), .clk(not_14_out), .Q(OutB), .Qn(t_ff_2_qn), .reset(not_15_out), .preset(not_13_out));
  not not_14 (not_14_out, not_6_out);
  not not_15 (not_15_out, nand_6_out);
  not not_16 (not_16_out, nand_2_out);
  T_Flip_Flop t_ff_3 (
    .T(or_3_out), .clk(not_17_out), .Q(OutC), .Qn(t_ff_3_qn), .reset(not_18_out), .preset(not_16_out));
  not not_17 (not_17_out, not_6_out);
  not not_18 (not_18_out, nand_7_out);
  nand nand_7 (nand_7_out, nand_2_out, not_5_out);
  not not_19 (not_19_out, nand_3_out);
  T_Flip_Flop t_ff_4 (
    .T(or_4_out), .clk(not_20_out), .Q(OutD), .Qn(t_ff_4_qn), .reset(not_21_out), .preset(not_19_out));
  not not_20 (not_20_out, not_6_out);
  not not_21 (not_21_out, nand_8_out);
  nand nand_8 (nand_8_out, nand_3_out, not_5_out);
endmodule

module SN74155 (
  input  SelectA,
  input  SelectB,
  input  C1,
  input  C2,
  input  G1,
  input  G2,
  output Y20,
  output Y21,
  output Y22,
  output Y23,
  output Y10,
  output Y11,
  output Y12,
  output Y13
);

  wire and_1_out, and_2_out, not_1_out, not_2_out, not_3_out, not_4_out, not_5_out, not_6_out, not_7_out,
       not_8_out, not_9_out;

  not not_1 (not_1_out, SelectB);
  not not_2 (not_2_out, SelectA);
  not not_3 (not_3_out, C1);
  not not_4 (not_4_out, not_1_out);
  not not_5 (not_5_out, not_2_out);
  not not_6 (not_6_out, G1);
  and and_1 (and_1_out, not_6_out, not_7_out);
  not not_7 (not_7_out, not_3_out);
  not not_8 (not_8_out, C2);
  and and_2 (and_2_out, not_8_out, not_9_out);
  not not_9 (not_9_out, G2);
  nand nand_1 (Y10, not_1_out, not_2_out, and_1_out);
  nand nand_2 (Y11, not_1_out, not_5_out, and_1_out);
  nand nand_3 (Y12, not_4_out, not_2_out, and_1_out);
  nand nand_4 (Y13, not_4_out, not_5_out, and_1_out);
  nand nand_5 (Y20, not_1_out, not_2_out, and_2_out);
  nand nand_6 (Y21, not_1_out, not_5_out, and_2_out);
  nand nand_7 (Y22, not_4_out, not_2_out, and_2_out);
  nand nand_8 (Y23, not_4_out, not_5_out, and_2_out);
endmodule

module Final_Control (
  input  PlayerOne,
  input  LedOne,
  input  LedEight,
  input  QD,
  input  ResetOne,
  output UpDown,
  output Load,
  output En,
  output G
);

  wire NA1_2_out, NA1_out, NA2_out, NA3_out, NA3_QD_out, NA4_out, NA5_out, NA8_QD_out, not_1_out, not_2_out,
       not_3_out, not_4_out, not_5_out, not_6_out, not_7_out, not_8_out, not_9_out;

  not not_1 (not_1_out, PlayerOne);
  not not_2 (not_2_out, LedOne);
  not not_3 (not_3_out, LedEight);
  not not_4 (not_4_out, ResetOne);
  not not_5 (not_5_out, not_1_out);
  not not_6 (not_6_out, not_2_out);
  nand NA1 (NA1_out, not_5_out, not_6_out);
  nand NA1_2 (NA1_2_out, NA1_out, NA2_out);
  not not_7 (not_7_out, not_3_out);
  nand NA2 (NA2_out, not_5_out, not_7_out);
  J_K_Flip_Flop #(.trigger("falling")) FlipFlop1 (
    .J(1'b1), .K(1'b1), .clk(NA1_2_out), .Q(UpDown), .reset(NA5_out));  // open: Qn, preset
  nand NA3 (NA3_out, not_5_out, not_2_out);
  nand NA3_QD (NA3_QD_out, NA3_out, not_8_out);
  not not_8 (not_8_out, QD);
  nand NA4 (NA4_out, NA3_QD_out, NA8_QD_out);
  nand NA5 (NA5_out, not_4_out, NA4_out);
  J_K_Flip_Flop #(.trigger("falling")) FlipFlop2 (
    .J(1'b1), .K(1'b1), .clk(not_9_out), .Q(Load), .Qn(En));  // open: preset, reset
  not not_9 (not_9_out, NA5_out);
  nand NA8_QD (NA8_QD_out, not_8_out, not_7_out);

  assign G = En;

  // Notes on the sheet:
  //   ΝΑ1: Player pushes the Button Player when the Led One is ON
  //   ΝΑ2: Player pushes the Button Player when the Led Eight is ON
  //   ΝΑ1_2: OR Gate that becomes True when Player wins! 
  //   We use NOT Gates in PlayerOne, ResetOne, LedOne, and LedEight to simulate the Negative - Pull Down Logic.
  //   FlipFlop1: Changes to adapt UpDown and keeps track of Direction!
  //   ΝΑ3: Player pushes the Button Player when the Led One is OFF
  //   NA3_QD: ON when (NA3 OR Player did not push the Button Player on Time) 
endmodule
